# Fritzing sketch ESP32_1.8_SPI_DISPLAY (saved by Fritzing 0.9.3b)

parts:
  A2 = Wemos S2 Mini [part_number="WeMos D1 Mini Lite"]
  Bauteil5 = TFT 1.8 inch 160x128 w microSD [part_number=358]

nets:
  N1: A2.Pin_2, Bauteil5.LITE
  N2: A2.Pin_3, Bauteil5.RESET
  N3: A2.Pin_4, Bauteil5.MISO
  N4: A2.Pin_5, Bauteil5.CARDCS, Bauteil5.TFTDC
  N5: A2.Pin_6, Bauteil5.SCLK, Bauteil5.MOSI
  N6: A2.Pin_7, Bauteil5.TFTCS
  N7: A2.Pin_8, Bauteil5.+5V
  N8: A2.Pin_18, A2.Pin_26, Bauteil5.GND

notes:
  Option A3

custom parts:
  Wemos S2 Mini: A mini wifi board based on the ESP32-S2FN4R2.
  TFT 1.8 inch 160x128 w microSD: This lovely little display breakout is the best way to add a small, colorful and bright display to any project. Since the display uses 4-wire SPI to communicate and has its own pixel-addressable frame buffer, it can be used with every kind of microcontroller. Even a very small one with low memory and few pins available! The 1.8" display has 128x160 color pixels.
