# Fritzing sketch ESP32_PIR_SENSOR (saved by Fritzing 0.9.3b)

parts:
  A1 = Wemos S2 Mini [part_number="WeMos D1 Mini Lite"]
  PIR1 = PIR sensor

nets:
  N1: A1.Pin_8, PIR1.VDD
  N2: A1.Pin_18, A1.Pin_26, PIR1.GND
  N3: A1.Pin_20, PIR1.SIG

custom parts:
  Wemos S2 Mini: A mini wifi board based on the ESP32-S2FN4R2.
